# Fritzing sketch circuit (saved by Fritzing 0.9.3b)

parts:
  Part1 = Arduino Uno (Rev3) - ICSP
  Part2 = Bluetooth HC-05 Macho
  S1 = Toggle Switch [package=THT]
  S2 = Toggle Switch [package=THT]
  C2 = Electrolytic Capacitor [capacitance=1μF package="0405 [SMD, electrolytic]"]
  S3 = Toggle Switch [package=THT]
  S4 = Toggle Switch [package=THT]

nets:
  N1: Part1.D0/RX, S1.L1
  N2: Part1.D1/TX, S2.L1
  N3: Part1.D4, S2.L2
  N4: Part1.D5_PWM, S1.L2
  N5: Part1.RESET, C2.-
  5V: Part1.5V, Part2.VCC
  GND: Part1.GND, Part2.GND
  N6: Part2.State, S3.L2
  N7: Part2.TXD, S1.COM
  N8: Part2.RXD, S2.COM
  N9: Part2.Key, S4.COM
  N10: C2.+, S3.COM

notes:
  10uf Capacitor
  3.3-6 HC-05
